# Fritzing sketch Arduino_74HC595-5101AS_schema (saved by Fritzing 0.9.2b)
breadboards: 2

parts:
  U1 = 74HC595 [package="DIP16 [THT]"]
  Composant1 = Arduino Uno (Rev3)
  7_Segment1 = 7 Segment Display
  U2 = Voltage Regulator [package=to220-adj]  # not connected
  R3 = Resistor [tolerance=±5% resistance=220 package=THT]
  R4 = Resistor [tolerance=±5% resistance=220 package=THT]
  R5 = Resistor [tolerance=±5% resistance=220 package=THT]
  R6 = Resistor [tolerance=±5% resistance=220 package=THT]
  R7 = Resistor [tolerance=±5% resistance=220 package=THT]
  R8 = Resistor [tolerance=±5% resistance=330 package=THT]
  R1 = Resistor [tolerance=±5% resistance=220 package=THT]
  R2 = Resistor [tolerance=±5% resistance=220 package=THT]
  S1 = Pushbutton [package="[THT]"]

nets:
  N1: U1.Q1, R1.Pin_0
  N2: U1.Q2, R2.Pin_0
  N3: U1.Q3, R3.Pin_0
  N4: U1.Q4, R4.Pin_0
  N5: U1.Q5, R5.Pin_0
  N6: U1.Q6, R6.Pin_0
  N7: U1.Q7, R7.Pin_0
  N8: U1.SH_CP, Composant1.D12/MISO
  N9: U1.ST_CP, Composant1.D11_PWM/MOSI
  N10: U1.DS, Composant1.D10_PWM/SS
  N11: U1.Q0, R8.Pin_0
  N12: Composant1.GND, Composant1.D2, 7_Segment1.common_cathode, S1.Pin_1, S1.Pin_2
  N13: 7_Segment1.Segment_E, R4.Pin_1
  N14: 7_Segment1.Segment_D, R3.Pin_1
  N15: 7_Segment1.Segment_C, R2.Pin_1
  N16: 7_Segment1.Segment_DP, R7.Pin_1
  N17: 7_Segment1.Segment_B, R1.Pin_1
  N18: 7_Segment1.Segment_A, R8.Pin_1
  N19: 7_Segment1.Segment_F, R5.Pin_1
  N20: 7_Segment1.Segment_G, R6.Pin_1
  N21: S1.Pin_3, S1.Pin_4
